// Logisim project branch-comp.circ as structural Verilog: 1 circuit, main circuit branch_comp
module branch_comp (
  input  [31:0] BrData1,
  input  [31:0] BrData2,
  input  BrUn,
  output BrEq,
  output BrLt
);

  wire comparator_1_eq, comparator_2_eq, comparator_3_lt, comparator_4_lt, multiplexer_1_out,
       multiplexer_3_out;

  Comparator #(.width(32)) comparator_1 (.a(BrData1), .b(BrData2), .eq(comparator_1_eq));  // open: gt, lt
  Comparator #(.mode("unsigned"), .width(32)) comparator_2 (
    .a(BrData1), .b(BrData2), .eq(comparator_2_eq));  // open: gt, lt
  Comparator #(.width(32)) comparator_3 (.a(BrData1), .b(BrData2), .lt(comparator_3_lt));  // open: gt, eq
  Comparator #(.mode("unsigned"), .width(32)) comparator_4 (
    .a(BrData1), .b(BrData2), .lt(comparator_4_lt));  // open: gt, eq
  Multiplexer multiplexer_1 (.in0(comparator_1_eq), .in1(comparator_2_eq), .out(multiplexer_1_out), .sel(BrUn));
  Multiplexer multiplexer_2 (.in0(1'b0), .in1(1'b1), .out(BrLt), .sel(multiplexer_3_out));
  Multiplexer multiplexer_3 (.in0(comparator_3_lt), .in1(comparator_4_lt), .out(multiplexer_3_out), .sel(BrUn));
  Multiplexer multiplexer_4 (.in0(1'b0), .in1(1'b1), .out(BrEq), .sel(multiplexer_1_out));

  // Notes on the sheet:
  //   INPUTS to your circuit
  //   signed
  //   Unsigned
  //   signed
  //   Unsigned
  //   DON'T CHANGE THE LOCATIONS OF THE INPUTS AND OUTPUTS!
  //   OUTPUT from your circuit
endmodule
