// Logisim project control-logic.circ as structural Verilog: 1 circuit, main circuit control_logic
module control_logic (
  input  [31:0] Instruction,
  input  BrEq,
  input  BrLt,
  output PCSel,
  output RegWEn,
  output [2:0] ImmSel,
  output BrUn,
  output ASel,
  output BSel,
  output [3:0] ALUSel,
  output MemWEn,
  output [1:0] WBSel
);

  wire and_8_out, and_9_out, and_10_out, and_11_out, and_14_out, and_15_out, and_16_out, and_17_out,
       and_21_out, and_22_out, and_25_out, Btype_PCSel, is_auipc, is_B_type, is_bgeu, is_bltu, is_I_type,
       is_J_type, is_lui, is_mul, is_mulh, is_mulhu, is_R_type, is_sraType, is_sub, is_U_type, not_1_out,
       not_2_out, not_3_out, not_4_out, or_2_out, or_3_out, or_4_out, or_5_out;
  wire [2:0] multiplexer_1_out, multiplexer_4_out, multiplexer_6_out, multiplexer_8_out, undriven;
  wire [3:0] bit_extender_1_out, bit_extender_2_out, ItypeSel, multiplexer_12_out, multiplexer_13_out,
       multiplexer_15_out, multiplexer_16_out, RtypeSel, special;

  and and_1 (is_I_type, Instruction[0], Instruction[1], ~Instruction[2], ~Instruction[3], Instruction[4], ~Instruction[5], ~Instruction[6]);  // AND_Gate
  and and_2 (is_R_type, Instruction[0], Instruction[1], ~Instruction[2], ~Instruction[3], Instruction[4], Instruction[5], ~Instruction[6]);  // AND_Gate
  and and_3 (is_B_type, Instruction[0], Instruction[1], ~Instruction[2], ~Instruction[3], ~Instruction[4], Instruction[5], Instruction[6]);  // AND_Gate
  and and_4 (is_auipc, Instruction[0], ~Instruction[1], ~Instruction[2], ~Instruction[3], Instruction[4], ~Instruction[5], ~Instruction[6]);  // AND_Gate
  and and_5 (is_lui, Instruction[0], Instruction[1], Instruction[2], ~Instruction[3], ~Instruction[4], Instruction[5], ~Instruction[6]);  // AND_Gate
  and and_6 (is_J_type, Instruction[0], Instruction[1], Instruction[2], Instruction[3], ~Instruction[4], Instruction[5], Instruction[6]);  // AND_Gate
  and and_7 (is_U_type, is_auipc, is_lui);
  not not_1 (not_1_out, is_R_type);
  and and_8 (and_8_out, ~Instruction[12], ~Instruction[13], ~Instruction[14]);  // AND_Gate
  and and_9 (and_9_out, ~Instruction[25], ~Instruction[26], ~Instruction[27], ~Instruction[28], ~Instruction[29], Instruction[30], ~Instruction[31]);  // AND_Gate
  and and_10 (and_10_out, Instruction[12], ~Instruction[13], Instruction[14]);  // AND_Gate
  and and_11 (and_11_out, ~Instruction[25], ~Instruction[26], ~Instruction[27], ~Instruction[28], ~Instruction[29], Instruction[30], ~Instruction[31]);  // AND_Gate
  Multiplexer #(.width(3)) multiplexer_1 (.in0(undriven), .in1(3'b100), .out(multiplexer_1_out), .sel(is_J_type));
  Multiplexer multiplexer_2 (.in0(1'b0), .in1(1'b1), .out(BSel), .sel(not_1_out));
  not not_2 (not_2_out, BrEq);
  Multiplexer #(.select(3)) multiplexer_3 (
    .in0(BrEq), .in1(not_2_out), .in4(BrLt), .in5(not_3_out), .in6(BrLt), .in7(not_4_out), .out(Btype_PCSel),
    .sel(Instruction[14:12]));  // open: in2, in3
  not not_3 (not_3_out, BrLt);
  not not_4 (not_4_out, BrLt);
  and and_12 (is_sub, is_R_type, and_8_out, and_9_out);
  and and_13 (is_sraType, and_10_out, and_11_out);
  or or_1 (RegWEn, is_I_type, is_R_type);
  Multiplexer #(.width(3)) multiplexer_4 (
    .in0(multiplexer_1_out), .in1(3'b011), .out(multiplexer_4_out), .sel(is_U_type));
  Multiplexer multiplexer_5 (.in0(1'b0), .in1(1'b1), .out(ASel), .sel(is_B_type));
  Multiplexer #(.width(3)) multiplexer_6 (
    .in0(multiplexer_4_out), .in1(3'b010), .out(multiplexer_6_out), .sel(is_B_type));
  Multiplexer multiplexer_7 (.in0(1'b0), .in1(Btype_PCSel), .out(PCSel), .sel(is_B_type));
  and and_14 (and_14_out, ~Instruction[12], ~Instruction[13], ~Instruction[14]);  // AND_Gate
  and and_15 (and_15_out, Instruction[25], ~Instruction[26], ~Instruction[27], ~Instruction[28], ~Instruction[29], ~Instruction[30], ~Instruction[31]);  // AND_Gate
  and and_16 (and_16_out, Instruction[12], ~Instruction[13], ~Instruction[14]);  // AND_Gate
  and and_17 (and_17_out, Instruction[25], ~Instruction[26], ~Instruction[27], ~Instruction[28], ~Instruction[29], ~Instruction[30], ~Instruction[31]);  // AND_Gate
  and and_18 (is_mul, is_R_type, and_14_out, and_15_out);
  and and_19 (is_mulh, is_R_type, and_16_out, and_17_out);
  Multiplexer #(.width(3)) multiplexer_8 (
    .in0(multiplexer_6_out), .in1(3'b001), .out(multiplexer_8_out), .sel(is_R_type));
  or or_2 (or_2_out, is_bgeu, is_bltu);
  Multiplexer #(.width(3)) multiplexer_9 (.in0(multiplexer_8_out), .in1(3'b000), .out(ImmSel), .sel(is_I_type));
  and and_20 (BrUn, is_B_type, or_2_out);
  and and_21 (and_21_out, Instruction[12], Instruction[13], ~Instruction[14]);  // AND_Gate
  and and_22 (and_22_out, Instruction[12], Instruction[13], Instruction[14]);
  and and_23 (is_mulhu, is_R_type, and_21_out);
  and and_24 (is_bgeu, is_B_type, and_22_out);
  assign bit_extender_1_out = {{1{1'b0}}, Instruction[14:12]};  // Bit_Extender bit_extender_1
  assign bit_extender_2_out = {{1{1'b0}}, Instruction[14:12]};  // Bit_Extender bit_extender_2
  or or_3 (or_3_out, is_mulh, is_mul);
  Multiplexer #(.width(4)) multiplexer_10 (.in0(bit_extender_1_out), .in1(4'b1101), .out(ItypeSel), .sel(is_sraType));
  Multiplexer #(.width(4)) multiplexer_11 (.in0(bit_extender_2_out), .in1(special), .out(RtypeSel), .sel(or_4_out));
  or or_4 (or_4_out, or_3_out, is_mulhu, or_5_out);
  or or_5 (or_5_out, is_sub, is_sraType);
  and and_25 (and_25_out, ~Instruction[12], Instruction[13], Instruction[14]);  // AND_Gate
  Multiplexer #(.width(4)) multiplexer_12 (.in1(4'b1101), .out(multiplexer_12_out), .sel(is_sraType));  // open: in0
  and and_26 (is_bltu, is_B_type, and_25_out);
  Multiplexer #(.width(4)) multiplexer_13 (
    .in0(multiplexer_12_out), .in1(4'b1011), .out(multiplexer_13_out), .sel(is_mulhu));
  Multiplexer #(.select(2), .width(4)) multiplexer_14 (
    .in0(4'b0000), .in1(RtypeSel), .in2(ItypeSel), .out(ALUSel), .sel({is_I_type, is_R_type}));  // open: in3
  Multiplexer #(.width(4)) multiplexer_15 (
    .in0(multiplexer_13_out), .in1(4'b1001), .out(multiplexer_15_out), .sel(is_mulh));
  Multiplexer #(.width(4)) multiplexer_16 (
    .in0(multiplexer_15_out), .in1(4'b1000), .out(multiplexer_16_out), .sel(is_mul));
  Multiplexer #(.width(4)) multiplexer_17 (.in0(multiplexer_16_out), .in1(4'b1100), .out(special), .sel(is_sub));

  // Other names for the same wires on the sheet: opcode[6:0] = Instruction[6:0]; rd[4:0] = Instruction[11:7];
  //   funct3[2:0] = Instruction[14:12]; rs1[4:0] = Instruction[19:15]; imm[11:0] = Instruction[31:20];
  //   rs2[4:0] = Instruction[24:20]; funct7[6:0] = Instruction[31:25]

  // Notes on the sheet:
  //   INPUTS to your circuit
  //   DON'T CHANGE THE LOCATIONS OF THE INPUTS AND OUTPUTS!
  //   OUTPUT from your circuit
  //   I类型特判
  //   R类型特判
endmodule
